// Digital circuit ROM8bit.dig as structural Verilog
module ROM8bit (
  input  in_2,
  output out_1,
  output [7:0] out_3,
  output out_4
);

  wire and_gate_1_out, and_gate_2_out, and_gate_3_out, and_gate_4_out, and_gate_5_out, and_gate_6_out,
       and_gate_7_out, and_gate_8_out, and_gate_9_out, and_gate_10_out, and_gate_11_out, and_gate_12_out,
       not_gate_1_out, not_gate_2_out, not_gate_3_out, not_gate_4_out, not_gate_5_out, not_gate_6_out,
       not_gate_7_out, not_gate_8_out, not_gate_9_out, not_gate_10_out, not_gate_11_out, not_gate_12_out,
       not_gate_13_out, not_gate_14_out, not_gate_15_out;

  program_counter program_counter_1 (.Clk(in_2), .Out(out_3));
  not_gate not_gate_1 (.A(out_3[0]), .Out(not_gate_1_out));
  not_gate not_gate_2 (.A(out_3[1]), .Out(not_gate_2_out));
  not_gate not_gate_3 (.A(out_3[2]), .Out(not_gate_3_out));
  not_gate not_gate_4 (.A(out_3[3]), .Out(not_gate_4_out));
  not_gate not_gate_5 (.A(out_3[4]), .Out(not_gate_5_out));
  not_gate not_gate_6 (.A(out_3[5]), .Out(not_gate_6_out));
  not_gate not_gate_7 (.A(out_3[6]), .Out(not_gate_7_out));
  not_gate not_gate_8 (.A(out_3[7]), .Out(not_gate_8_out));
  not_gate not_gate_9 (.A(1'b0), .Out(not_gate_9_out));
  not_gate not_gate_10 (.A(1'b0), .Out(not_gate_10_out));
  not_gate not_gate_11 (.A(1'b0), .Out(not_gate_11_out));
  not_gate not_gate_12 (.A(1'b0), .Out(not_gate_12_out));
  not_gate not_gate_13 (.A(1'b0), .Out(not_gate_13_out));
  not_gate not_gate_14 (.A(1'b0), .Out(not_gate_14_out));
  not_gate not_gate_15 (.A(1'b0), .Out(not_gate_15_out));
  and_gate and_gate_1 (.A(not_gate_1_out), .B(not_gate_2_out), .Out(and_gate_1_out));
  and_gate and_gate_2 (.A(1'b0), .B(not_gate_9_out), .Out(and_gate_2_out));
  and_gate and_gate_3 (.A(and_gate_1_out), .B(not_gate_3_out), .Out(and_gate_3_out));
  and_gate and_gate_4 (.A(and_gate_2_out), .B(not_gate_10_out), .Out(and_gate_4_out));
  and_gate and_gate_5 (.A(and_gate_3_out), .B(not_gate_4_out), .Out(and_gate_5_out));
  and_gate and_gate_6 (.A(and_gate_4_out), .B(not_gate_11_out), .Out(and_gate_6_out));
  and_gate and_gate_7 (.A(and_gate_5_out), .B(not_gate_5_out), .Out(and_gate_7_out));
  and_gate and_gate_8 (.A(and_gate_6_out), .B(not_gate_12_out), .Out(and_gate_8_out));
  and_gate and_gate_9 (.A(and_gate_7_out), .B(not_gate_6_out), .Out(and_gate_9_out));
  and_gate and_gate_10 (.A(and_gate_8_out), .B(not_gate_13_out), .Out(and_gate_10_out));
  and_gate and_gate_11 (.A(and_gate_9_out), .B(not_gate_7_out), .Out(and_gate_11_out));
  and_gate and_gate_12 (.A(and_gate_10_out), .B(not_gate_14_out), .Out(and_gate_12_out));
  and_gate and_gate_13 (.A(and_gate_11_out), .B(not_gate_8_out), .Out(out_1));
  and_gate and_gate_14 (.A(and_gate_12_out), .B(not_gate_15_out), .Out(out_4));
endmodule
